# Fritzing sketch basic (saved by Fritzing 0.9.2b)
breadboards: 1

parts:
  Raspberry_Pi_B_rev1 = Raspberry Pi B rev1
  IC1 = MCP3008 8-channel 10-bit ADC [part_number=MCP3008]
  KY-2 = Keyes Relay [package=THT]
  T1 = TMP36 Temperature Sensor [package="TO92 [THT]"]
  Analouge_Moisture_Sensor = Soil Moisture Sensor
  Water_Pump = DC Motor
  Power_plug1 = Power plug
  R1 = Resistor [tolerance=±5% resistance=220 package="0603 [SMD]"]

nets:
  N1: Raspberry_Pi_B_rev1.3V3, IC1.no_name_yet#15, IC1.no_name_yet#16, KY-2.power, T1.+Vs, Analouge_Moisture_Sensor.Pin_2, R1.Pin_0
  GND: Raspberry_Pi_B_rev1.GND, IC1.no_name_yet#9, IC1.no_name_yet#14, KY-2.ground, T1.GND, Analouge_Moisture_Sensor.Pin_1
  N2: Raspberry_Pi_B_rev1.GPIO_17, KY-2.signal, R1.Pin_1
  N3: Raspberry_Pi_B_rev1.GPIO_10, IC1.no_name_yet#11
  N4: Raspberry_Pi_B_rev1.GPIO_9, IC1.no_name_yet#12
  N5: Raspberry_Pi_B_rev1.GPIO_11, IC1.no_name_yet#13
  N6: Raspberry_Pi_B_rev1.GPIO_8, IC1.no_name_yet#10
  N7: IC1.no_name_yet#1, T1.Vout
  N8: KY-2.C, Power_plug1.VCC
  N9: KY-2.NO, Water_Pump.pin_2
  N10: Water_Pump.pin_1, Power_plug1.GND

custom parts:
  Keyes Relay: The Keyes 5V relay module is suitable for SCM development, home appliance control. It uses a 5V~12V TIL control signal which can control DC / AC signal.
